// Logisim project estagioID_EX.circ as structural Verilog: 1 circuit, main circuit estagioID_EX
module estagioID_EX (
  input  [31:0] PCplus4_ID,
  input  [31:0] opcode_ID,
  input  [31:0] RegWrite_ID,
  input  [31:0] Lui_ID,
  input  [31:0] rs1_ID,
  input  [31:0] ALUSrcB_ID,
  input  [31:0] MemToReg_ID,
  input  CLK,
  input  Clear,
  input  [31:0] rs2_ID,
  input  [31:0] PCSrc_ID,
  input  [31:0] MemRead_ID,
  input  Enable,
  input  [31:0] rd_ID,
  input  [31:0] Jump_ID,
  input  [31:0] MemWrite_ID,
  input  [31:0] f3_ID,
  input  [31:0] Jalr_ID,
  input  [31:0] Branch_ID,
  input  [31:0] f7_ID,
  input  [31:0] ALUOp_ID,
  input  [31:0] BranchSrc_ID,
  input  [31:0] imm_ID,
  input  [31:0] Auipc_ID,
  output [31:0] PCplus4_EX,
  output [31:0] opcode_EX,
  output [31:0] RegWrite_EX,
  output [31:0] Lui_EX,
  output [31:0] rs1_EX,
  output [31:0] ALUSrcB_EX,
  output [31:0] MemToReg_EX,
  output [31:0] rs2_EX,
  output [31:0] PCSrc_EX,
  output [31:0] MemRead_EX,
  output [31:0] rd_EX,
  output [31:0] Jump_EX,
  output [31:0] MemWrite_EX,
  output [31:0] f3_EX,
  output [31:0] Jalr_EX,
  output [31:0] Branch_EX,
  output [31:0] f7_EX,
  output [31:0] ALUOp_EX,
  output [31:0] BranchSrc_EX,
  output [31:0] imm_EX,
  output [31:0] Auipc_EX
);

  Register #(.width(32)) PCplus4 (.D(PCplus4_ID), .en(Enable), .clk(CLK), .Q(PCplus4_EX), .clr(Clear));
  Register #(.width(32)) opcode (.D(opcode_ID), .en(Enable), .clk(CLK), .Q(opcode_EX), .clr(Clear));
  Register #(.width(32)) rs1 (.D(rs1_ID), .en(Enable), .clk(CLK), .Q(rs1_EX));  // open: clr
  Register #(.width(32)) rs2 (.D(rs2_ID), .en(Enable), .clk(CLK), .Q(rs2_EX), .clr(Clear));
  Register #(.width(32)) rd (.D(rd_ID), .en(Enable), .clk(CLK), .Q(rd_EX), .clr(Clear));
  Register #(.width(32)) funct3 (.D(f3_ID), .en(Enable), .clk(CLK), .Q(f3_EX), .clr(Clear));
  Register #(.width(32)) funct7 (.D(f7_ID), .en(Enable), .clk(CLK), .Q(f7_EX), .clr(Clear));
  Register #(.width(32)) imm (.D(imm_ID), .en(Enable), .clk(CLK), .Q(imm_EX), .clr(Clear));
  Register #(.width(32)) RegWrite (.D(RegWrite_ID), .en(Enable), .clk(CLK), .Q(RegWrite_EX), .clr(Clear));
  Register #(.width(32)) ALUSrc (.D(ALUSrcB_ID), .en(Enable), .clk(CLK), .Q(ALUSrcB_EX));  // open: clr
  Register #(.width(32)) PCSrc (.D(PCSrc_ID), .en(Enable), .clk(CLK), .Q(PCSrc_EX), .clr(Clear));
  Register #(.width(32)) Jump (.D(Jump_ID), .en(Enable), .clk(CLK), .Q(Jump_EX), .clr(Clear));
  Register #(.width(32)) Jalr (.D(Jalr_ID), .en(Enable), .clk(CLK), .Q(Jalr_EX), .clr(Clear));
  Register #(.width(32)) ALUOp (.D(ALUOp_ID), .en(Enable), .clk(CLK), .Q(ALUOp_EX), .clr(Clear));
  Register #(.width(32)) Auipc (.D(Auipc_ID), .en(Enable), .clk(CLK), .Q(Auipc_EX), .clr(Clear));
  Register #(.width(32)) MemRead (.D(MemRead_ID), .en(Enable), .clk(CLK), .Q(MemRead_EX), .clr(Clear));
  Register #(.width(32)) Branch (.D(Branch_ID), .en(Enable), .clk(CLK), .Q(Branch_EX), .clr(Clear));
  Register #(.width(32)) BranchSrc (.D(BranchSrc_ID), .en(Enable), .clk(CLK), .Q(BranchSrc_EX), .clr(Clear));
  Register #(.width(32)) Lui (.D(Lui_ID), .en(Enable), .clk(CLK), .Q(Lui_EX), .clr(Clear));
  Register #(.width(32)) MemToReg (.D(MemToReg_ID), .en(Enable), .clk(CLK), .Q(MemToReg_EX), .clr(Clear));
  Register #(.width(32)) MemWrite (.D(MemWrite_ID), .en(Enable), .clk(CLK), .Q(MemWrite_EX), .clr(Clear));

  // Notes on the sheet:
  //   PC
  //   Decodificador
  //   ucPrincipal e ucDesvio
endmodule
