// Logisim project estagioIF_ID.circ as structural Verilog: 1 circuit, main circuit estagioIF_ID
module estagioIF_ID (
  input  CLK,
  input  Clear,
  input  Enable,
  input  [31:0] Instrucao_IF,
  input  [31:0] PCplus4_IF,
  output [31:0] Instrucao_ID,
  output [31:0] PCplus4_ID
);

  Register #(.width(32)) PCplus4 (.D(PCplus4_IF), .en(Enable), .clk(CLK), .Q(PCplus4_ID), .clr(Clear));
  Register #(.width(32)) Instrucao (.D(Instrucao_IF), .en(Enable), .clk(CLK), .Q(Instrucao_ID), .clr(Clear));
endmodule
