// Logisim project ucEncaminhamento.circ as structural Verilog: 1 circuit, main circuit ucEncaminhamento
module ucEncaminhamento (
  input  [4:0] rs1,
  input  [4:0] rs2,
  input  [4:0] rd_MEM,
  input  RegWrite_MEM,
  input  [4:0] rd_WB,
  input  RegWrite_WB,
  output [1:0] ForwardA,
  output [1:0] ForwardB
);

  wire comparator_1_eq, comparator_2_eq, comparator_3_eq, comparator_4_eq, comparator_5_eq, comparator_6_eq,
       escreveMEM, escreveWB;

  Comparator #(.width(5)) comparator_1 (.a(rd_MEM), .b({5{1'b0}}), .eq(comparator_1_eq));  // open: gt, lt
  Comparator #(.width(5)) comparator_2 (.a(rd_WB), .b({5{1'b0}}), .eq(comparator_2_eq));  // open: gt, lt
  and and_1 (escreveMEM, RegWrite_MEM, ~comparator_1_eq);  // AND_Gate
  and and_2 (escreveWB, RegWrite_WB, ~comparator_2_eq);  // AND_Gate
  Comparator #(.width(5)) comparator_3 (.a(rd_MEM), .b(rs1), .eq(comparator_3_eq));  // open: gt, lt
  Comparator #(.width(5)) comparator_4 (.a(rd_MEM), .b(rs2), .eq(comparator_4_eq));  // open: gt, lt
  and and_3 (ForwardA[1], escreveMEM, comparator_3_eq);
  and and_4 (ForwardB[1], escreveMEM, comparator_4_eq);
  Comparator #(.width(5)) comparator_5 (.a(rd_WB), .b(rs1), .eq(comparator_5_eq));  // open: gt, lt
  Comparator #(.width(5)) comparator_6 (.a(rd_WB), .b(rs2), .eq(comparator_6_eq));  // open: gt, lt
  and and_5 (ForwardA[0], escreveWB, comparator_5_eq, ~ForwardA[1]);  // AND_Gate
  and and_6 (ForwardB[0], escreveWB, comparator_6_eq, ~ForwardB[1]);  // AND_Gate

  // Other names for the same wires on the sheet: memA = ForwardA[0]; exA = ForwardA[1]; memB = ForwardB[0];
  //   exB = ForwardB[1]

  // Notes on the sheet:
  //   Entradas
  //   Escrita válida
  //   Conflito no EX
  //   Conflito no MEM
  //   Saídas
endmodule
