// Logisim project ucULA.circ as structural Verilog: 1 circuit, main circuit ucULA
module ucULA (
  input  [2:0] funct3,
  input  [6:0] opcode,
  input  [1:0] ALUOp,
  input  [6:0] funct7,
  output [2:0] ALUControl,
  output sraiSeletor,
  output subSeletor
);

  wire and_1_out, and_2_out;
  wire [2:0] multiplexer_1_out, multiplexer_2_out;

  Multiplexer #(.width(3)) multiplexer_1 (.in0(3'b010), .in1(3'b011), .out(multiplexer_1_out), .sel(funct3[1]));
  and and_1 (and_1_out, funct7[5], opcode[5], ALUOp[1]);
  Multiplexer #(.width(3)) multiplexer_2 (
    .in0(3'b000), .in1(multiplexer_1_out), .out(multiplexer_2_out), .sel(funct3[2]));
  and and_2 (and_2_out, ~ALUOp[1], ALUOp[0]);  // AND_Gate
  or or_1 (subSeletor, and_1_out, and_2_out);
  Multiplexer #(.select(2), .width(3)) multiplexer_3 (
    .in0(3'b000), .in1(multiplexer_2_out), .in2(funct3), .out(ALUControl), .sel(ALUOp));  // open: in3

  assign sraiSeletor = funct7[5];

  // Notes on the sheet:
  //   blt/bge
  //   bltu/bgeu
  //   funct3 >= 0x4
  //   beq/bne
  //   R-type/I-type
  //   load/store
  //   B-type
  //   ALUOp = 01
  //   Branch
endmodule
