// Logisim project main.circ as structural Verilog: 1 circuit, main circuit main
module main (
);

  wire and_1_out, and_2_out, and_3_out, and_4_out, Branch_EX, BranchSrc, CLK, estagioex_mem_1_jump_mem,
       estagioex_mem_1_memread_mem, estagioex_mem_1_memtoreg_mem, estagioex_mem_1_memwrite_mem,
       estagioex_mem_1_regwrite_mem, estagioid_ex_1_p22, estagioid_ex_1_p24, estagioid_ex_1_p27,
       estagioid_ex_1_p28, estagioid_ex_1_p29, estagioid_ex_1_p32, estagioid_ex_1_p33, estagioid_ex_1_p34,
       estagioid_ex_1_p35, estagioid_ex_1_p36, estagioid_ex_1_p37, estagioid_ex_1_p42, estagioid_ex_1_p45,
       estagioid_ex_1_p47, estagioif_id_1_p5, estagioif_id_1_p7, estagioif_id_1_p8, estagiomem_wb_1_jump_wb,
       estagiomem_wb_1_memtoreg_wb, Jalr_EX, Jump_EX, PCSrc_EX, PCSrc_EX_nao_usado, RegWrite_WB, Stop,
       sUnsigned, ucprincipal_1_alusrcb, ucprincipal_1_auipc_uc, ucprincipal_1_branch, ucprincipal_1_jump,
       ucprincipal_1_lui_uc, ucprincipal_1_memread, ucprincipal_1_memtoreg, ucprincipal_1_memwrite,
       ucprincipal_1_pcsrc, ucprincipal_1_regwrite, ucprincipal_1_s_jalr, Zero;
  wire [1:0] offset, ucenderecamento_1_size, ucprincipal_1_aluop;
  wire [2:0] decodificador_1_funct3, estagioex_mem_1_f3_mem, estagioid_ex_1_p44;
  wire [3:0] ucenderecamento_1_byteenable, ucula_1_p5;
  wire [4:0] decodificador_1_rd, decodificador_1_rs1, decodificador_1_rs2, estagioex_mem_1_rd_mem,
       estagioid_ex_1_p43, rd_WB;
  wire [6:0] decodificador_1_funct7, decodificador_1_opcode;
  wire [31:0] adder_1_out, addrBranch, ALU, ALU_EX, bancoregistradores_1_ld1, bancoregistradores_1_ld2,
       contadorciclos_1_contador, decodificador_1_imm, estagioex_mem_1_ld2_mem, estagioex_mem_1_pcplus4_mem,
       estagioid_ex_1_p26, estagioid_ex_1_p40, estagioid_ex_1_p41, estagioid_ex_1_p46, estagioif_id_1_p9,
       estagiomem_wb_1_aluresult_wb, estagiomem_wb_1_memdata_wb, estagiomem_wb_1_pcplus4_wb, Imm, LD1, LD2,
       memdados_1_dados_lidos, meminstr_1_instruction, multiplexer_1_out, multiplexer_2_out,
       multiplexer_3_out, multiplexer_5_out, multiplexer_6_out, PC, PC_q, WD_WB;

  Multiplexer #(.width(32)) multiplexer_1 (
    .in0(adder_1_out), .in1(addrBranch), .out(multiplexer_1_out), .sel(PCSrc_EX));
  // Probe on Imm
  and and_1 (and_1_out, CLK, ~Stop);  // AND_Gate
  // Probe on contadorciclos_1_contador
  contadorCiclos contadorciclos_1 (.Clock(and_1_out), .Contador(contadorciclos_1_contador));
  Clock clock_1 (.out(CLK));
  Register #(.width(32)) u_PC (.D(multiplexer_2_out), .en(and_2_out), .clk(and_2_out), .Q(PC_q));  // open: clr
  Multiplexer #(.width(32)) multiplexer_2 (
    .in0(multiplexer_1_out), .in1(ALU_EX), .out(multiplexer_2_out), .sel(Jalr_EX));
  and and_2 (and_2_out, CLK, ~Stop);  // AND_Gate
  // Probe on PC
  // Probe on LD1
  // Probe on LD2
  // Probe on ALU
  Adder #(.width(32)) adder_1 (.a(32'h4), .b(PC_q), .out(adder_1_out));  // open: cin, cout
  memInstr meminstr_1 (.PC_address(PC_q), .Instruction(meminstr_1_instruction));
  // estagioIF_ID estagioif_id_1: pin names not known; wires that end beside it: adder_1_out, meminstr_1_instruction, PC_q, CLK, estagioif_id_1_p5, estagioif_id_1_p5, estagioif_id_1_p7, estagioif_id_1_p8, estagioif_id_1_p9
  decodificador decodificador_1 (
    .instrucao(estagioif_id_1_p9), .imm(decodificador_1_imm), .opcode(decodificador_1_opcode),
    .rd(decodificador_1_rd), .funct3(decodificador_1_funct3), .rs1(decodificador_1_rs1),
    .rs2(decodificador_1_rs2), .funct7(decodificador_1_funct7));
  ucPrincipal ucprincipal_1 (
    .BranchSrc(BranchSrc), .opcode(decodificador_1_opcode), .MemRead(ucprincipal_1_memread),
    .MemWrite(ucprincipal_1_memwrite), .Jump(ucprincipal_1_jump), .Branch(ucprincipal_1_branch),
    .S_Jalr(ucprincipal_1_s_jalr), .RegWrite(ucprincipal_1_regwrite), .ALUOp(ucprincipal_1_aluop),
    .Auipc_uc(ucprincipal_1_auipc_uc), .ALUSrcB(ucprincipal_1_alusrcb), .Lui_uc(ucprincipal_1_lui_uc),
    .Stop(Stop), .MemToReg(ucprincipal_1_memtoreg), .PCSrc(ucprincipal_1_pcsrc));
  bancoRegistradores bancoregistradores_1 (
    .WD(WD_WB), .WR(rd_WB), .LD1(bancoregistradores_1_ld1), .LR1(decodificador_1_rs1),
    .LD2(bancoregistradores_1_ld2), .LR2(decodificador_1_rs2), .clk(CLK), .RegWrite(RegWrite_WB));
  idULA idula_1 (
    .A(bancoregistradores_1_ld1), .B(bancoregistradores_1_ld2), .funct3(decodificador_1_funct3), .Zero(Zero));
  ucDesvio ucdesvio_1 (.Zero(Zero), .funct3(decodificador_1_funct3), .BranchSrc(BranchSrc));
  // estagioID_EX estagioid_ex_1: pin names not known; wires that end beside it: estagioif_id_1_p7, estagioif_id_1_p8, ucprincipal_1_auipc_uc, ucprincipal_1_lui_uc, ucprincipal_1_pcsrc, ucprincipal_1_jump, ucprincipal_1_aluop, ucprincipal_1_regwrite, ucprincipal_1_alusrcb, ucprincipal_1_memtoreg, ucprincipal_1_memread, ucprincipal_1_memwrite, ucprincipal_1_branch, ucprincipal_1_s_jalr, bancoregistradores_1_ld1, bancoregistradores_1_ld2, decodificador_1_opcode, decodificador_1_rd, decodificador_1_funct3, decodificador_1_funct7, decodificador_1_imm, estagioid_ex_1_p22, CLK, estagioid_ex_1_p24, estagioid_ex_1_p24, estagioid_ex_1_p26, estagioid_ex_1_p27, estagioid_ex_1_p28, estagioid_ex_1_p29, PCSrc_EX_nao_usado, Jump_EX, estagioid_ex_1_p32, estagioid_ex_1_p33, estagioid_ex_1_p34, estagioid_ex_1_p35, estagioid_ex_1_p36, estagioid_ex_1_p37, Branch_EX, Jalr_EX, estagioid_ex_1_p40, estagioid_ex_1_p41, estagioid_ex_1_p42, estagioid_ex_1_p43, estagioid_ex_1_p44, estagioid_ex_1_p45, estagioid_ex_1_p46, estagioid_ex_1_p47
  Multiplexer #(.width(32)) multiplexer_3 (
    .in0(estagioid_ex_1_p40), .in1(estagioid_ex_1_p26), .out(multiplexer_3_out), .sel(estagioid_ex_1_p28));
  Adder #(.width(32)) adder_2 (.a(estagioid_ex_1_p26), .b(estagioid_ex_1_p46), .out(addrBranch));  // open: cin, cout
  Multiplexer #(.width(32)) multiplexer_4 (
    .in0(estagioid_ex_1_p41), .in1(estagioid_ex_1_p46), .out(LD2), .sel(estagioid_ex_1_p34));
  Multiplexer #(.width(32)) multiplexer_5 (
    .in0(multiplexer_3_out), .in1({32{1'b0}}), .out(multiplexer_5_out), .sel(estagioid_ex_1_p29));
  // ucULA ucula_1: pin names not known; wires that end beside it: estagioid_ex_1_p42, estagioid_ex_1_p44, estagioid_ex_1_p45, estagioid_ex_1_p32, ucula_1_p5
  ULA ula_1 (.B(LD2), .ALUControl(ucula_1_p5), .A(multiplexer_5_out), .Result(ALU_EX));  // open: sZero
  and and_3 (and_3_out, Branch_EX, BranchSrc);
  or or_1 (PCSrc_EX, Jump_EX, and_3_out);
  estagioEX_MEM estagioex_mem_1 (
    .CLK(CLK), .ALUResult_EX(ALU_EX), .ld2_EX(estagioid_ex_1_p41), .rd_EX(estagioid_ex_1_p43),
    .f3_EX(estagioid_ex_1_p44), .MemRead_MEM(estagioex_mem_1_memread_mem),
    .MemWrite_MEM(estagioex_mem_1_memwrite_mem), .RegWrite_MEM(estagioex_mem_1_regwrite_mem),
    .MemToReg_MEM(estagioex_mem_1_memtoreg_mem), .Jump_MEM(estagioex_mem_1_jump_mem), .ALUResult_MEM(ALU),
    .ld2_MEM(estagioex_mem_1_ld2_mem), .rd_MEM(estagioex_mem_1_rd_mem),
    .PCplus4_MEM(estagioex_mem_1_pcplus4_mem), .f3_MEM(estagioex_mem_1_f3_mem));  // open: MemRead_EX, MemWrite_EX, RegWrite_EX, MemToReg_EX, Jump_EX, PCplus4_EX
  ucEnderecamento ucenderecamento_1 (
    .Adress(ALU), .Funct3(estagioex_mem_1_f3_mem), .writeEnable(estagioex_mem_1_memwrite_mem),
    .byteEnable(ucenderecamento_1_byteenable), .Size(ucenderecamento_1_size), .Offset(offset),
    .signal_unsigned(sUnsigned));
  and and_4 (and_4_out, CLK, ~Stop);  // AND_Gate
  memDados memdados_1 (
    .Endereco(ALU), .clk(and_4_out), .MemRead(estagioex_mem_1_memread_mem),
    .byteEnable(ucenderecamento_1_byteenable), .dado(estagioex_mem_1_ld2_mem), .size(ucenderecamento_1_size),
    .offset(offset), .sUnsigned(sUnsigned), .Dados_lidos(memdados_1_dados_lidos));
  estagioMEM_WB estagiomem_wb_1 (
    .RegWrite_MEM(estagioex_mem_1_regwrite_mem), .MemToReg_MEM(estagioex_mem_1_memtoreg_mem),
    .Jump_MEM(estagioex_mem_1_jump_mem), .CLK(CLK), .MemData_MEM(memdados_1_dados_lidos),
    .ALUResult_MEM(ALU), .rd_MEM(estagioex_mem_1_rd_mem), .PCplus4_MEM(estagioex_mem_1_pcplus4_mem),
    .RegWrite_WB(RegWrite_WB), .MemToReg_WB(estagiomem_wb_1_memtoreg_wb), .Jump_WB(estagiomem_wb_1_jump_wb),
    .MemData_WB(estagiomem_wb_1_memdata_wb), .ALUResult_WB(estagiomem_wb_1_aluresult_wb), .rd_WB(rd_WB),
    .PCplus4_WB(estagiomem_wb_1_pcplus4_wb));
  Multiplexer #(.width(32)) multiplexer_6 (
    .in0(estagiomem_wb_1_aluresult_wb), .in1(estagiomem_wb_1_memdata_wb), .out(multiplexer_6_out),
    .sel(estagiomem_wb_1_memtoreg_wb));
  Multiplexer #(.width(32)) multiplexer_7 (
    .in0(multiplexer_6_out), .in1(estagiomem_wb_1_pcplus4_wb), .out(WD_WB), .sel(estagiomem_wb_1_jump_wb));

  // Notes on the sheet:
  //   PC
  //   PC + 4
  //   AUIPC
  //   LUI
  //   PCSrc
  //   Jump
  //   AluOP
  //   RegWrite
  //   ALUSrc_B
  //   MemToReg
  //   MemRead
  //   MemWrite
  //   ID1_EX
  //   ID2_EX
  //   rd
  //   f3
  //   f7
  //   IMM
  //   rs2
  //   PCSrc
  //   memToReg
  //   Pc+4
  //   RD
  //   RegWrite
  //   Jump
  //   memRead
  //   ALU
  //   ID2
  //   MemWrite
  //   f3
  //   ALU
  //   LD
  //   memToReg
  //   Pc+4
  //   Jump
endmodule
