// Logisim project ImmGen.circ as structural Verilog: 1 circuit, main circuit immGen
module immGen (
  input  [31:0] instruction,
  input  [1:0] ImmSrc,
  output [31:0] imm
);

  wire [31:0] \extensorsinal_12_1_saída , \extensorsinal_12_2_saída , \extensorsinal_13_1_saída ,
       \extensorsinal_21_1_saída ;

  extensorSinal_12 extensorsinal_12_1 (.entrada(instruction[31:20]), .\saída (\extensorsinal_12_1_saída ));
  extensorSinal_12 extensorsinal_12_2 (
    .entrada({instruction[31:25], instruction[11:7]}), .\saída (\extensorsinal_12_2_saída ));
  extensorSinal_13 extensorsinal_13_1 (
    .entrada({instruction[31], instruction[7], instruction[30:25], instruction[11:8], 1'b0}),
    .\saída (\extensorsinal_13_1_saída ));
  extensorSinal_21 extensorsinal_21_1 (
    .entrada({instruction[31], instruction[19:12], instruction[20], instruction[30:21], 1'b0}),
    .\saída (\extensorsinal_21_1_saída ));
  extensorSinal_20 extensorsinal_20_1 (.entrada(instruction[31:12]));  // open: saída
  // Probe on imm
  Multiplexer #(.select(2), .width(32)) multiplexer_1 (
    .in0(\extensorsinal_12_1_saída ), .in1(\extensorsinal_12_2_saída ), .in2(\extensorsinal_13_1_saída ),
    .in3(\extensorsinal_21_1_saída ), .out(imm), .sel(ImmSrc));

  // Other names for the same wires on the sheet: B_type_imm[12:1] = {instruction[31], instruction[7], instruction[30:25], instruction[11:8]};
  //   imm_5[4:0] = instruction[11:7]; S_type_imm[11:0] = {instruction[31:25], instruction[11:7]};
  //   I_type_imm[11:0] = instruction[31:20]; imm_12[11:0] = instruction[31:20]; imm_20[19:0] = instruction[31:12];
  //   J_type_imm[20:1] = {instruction[31], instruction[19:12], instruction[20], instruction[30:21]};
  //   U_type_imm[19:0] = instruction[31:12]; imm_7[6:0] = instruction[31:25]

  // Notes on the sheet:
  //   Tipo I
  //   Tipo S
  //   Tipo B
  //   Tipo U
  //   Tipo J
endmodule
