// Logisim project extensoresSinal.circ as structural Verilog: 5 circuits, main circuit extensorSinal_16
module extensorSinal_16 (
  input  [15:0] entrada,
  output [31:0] saida
);

  // Probe on entrada
  // Probe on {entrada, {16{saida[15]}}}

  assign {saida[31:16], saida[14:0]} = {entrada, {15{saida[15]}}};
endmodule

module extensorSinal_12 (
  input  [11:0] entrada,
  output [31:0] saida
);

  // Probe on entrada
  // Probe on {{21{entrada[11]}}, entrada[10:0]}

  assign saida = {{21{entrada[11]}}, entrada[10:0]};
endmodule

module extensorSinal_13 (
  input  [12:0] entrada,
  output [31:0] saida
);

  // Probe on entrada
  // Probe on {{20{entrada[12]}}, entrada[11:0]}

  assign saida = {{20{entrada[12]}}, entrada[11:0]};
endmodule

module extensorSinal_20 (
  input  [19:0] entrada,
  output [31:0] saida
);

  // Probe on entrada
  // Probe on {{13{entrada[19]}}, entrada[18:0]}

  assign saida = {{13{entrada[19]}}, entrada[18:0]};
endmodule

module extensorSinal_21 (
  input  [20:0] entrada,
  output [31:0] saida
);

  // Probe on entrada
  // Probe on {{12{entrada[20]}}, entrada[19:0]}

  assign saida = {{12{entrada[20]}}, entrada[19:0]};
endmodule
