// Logisim project main.circ as structural Verilog: 1 circuit, main circuit main
module main (
);

  wire ALUSrc, and_1_out, and_2_out, and_3_out, Branch, BranchSrc, CLK, Jalr, Jump, MemRead, MemToReg,
       MemWrite, Neg, PCSrc, RegWrite, Stop, Zero;
  wire [1:0] ALUOp, ImmSrc;
  wire [2:0] decodificador_1_funct3;
  wire [3:0] ucula_1_alucontrol;
  wire [4:0] decodificador_1_rd, decodificador_1_rs1, decodificador_1_rs2;
  wire [6:0] decodificador_1_funct7, decodificador_1_opcode;
  wire [31:0] adder_1_out, ALU, bancoregistradores_1_ld2, contador_1_contador, datamem_1_dados_lidos, Imm,
       LD1, LD2, meminstr_1_instruction, multiplexer_1_out, multiplexer_2_out, multiplexer_3_out, PC,
       PC_4_b16e401b, WD;

  Adder #(.width(32)) adder_1 (.a(PC), .b(Imm), .out(adder_1_out));  // open: cin, cout
  and and_1 (and_1_out, CLK, ~Stop);  // AND_Gate
  Multiplexer #(.width(32)) multiplexer_1 (
    .in0(PC_4_b16e401b), .in1(adder_1_out), .out(multiplexer_1_out), .sel(PCSrc));
  // Probe on Imm
  contador contador_1 (.Clock(and_1_out), .Contador(contador_1_contador));
  Clock clock_1 (.out(CLK));
  Register #(.width(32)) u_PC (.D(multiplexer_2_out), .en(1'b1), .clk(and_2_out), .Q(PC));  // open: clr
  Multiplexer #(.width(32)) multiplexer_2 (.in0(multiplexer_1_out), .in1(ALU), .out(multiplexer_2_out), .sel(Jalr));
  and and_2 (and_2_out, CLK, ~Stop);  // AND_Gate
  // Probe on contador_1_contador
  // Probe on PC
  // Probe on LD1
  // Probe on LD2
  // Probe on ALU
  Adder #(.width(32)) adder_2 (.a(32'h4), .b(PC), .out(PC_4_b16e401b));  // open: cin, cout
  MemInstr meminstr_1 (.PC_address(PC), .Instruction(meminstr_1_instruction));
  decodificador decodificador_1 (
    .instruction(meminstr_1_instruction), .opcode(decodificador_1_opcode), .rd(decodificador_1_rd),
    .funct3(decodificador_1_funct3), .rs1(decodificador_1_rs1), .rs2(decodificador_1_rs2),
    .funct7(decodificador_1_funct7));
  // Probe on decodificador_1_opcode
  immGen immgen_1 (.\instrução (meminstr_1_instruction), .imm(Imm), .ImmSrc(ImmSrc));
  // Probe on decodificador_1_rs1
  // Probe on decodificador_1_rs2
  ucBranch_main main_1 (.Zero(Zero), .Neg(Neg), .funct3(decodificador_1_funct3), .BranchSrc(BranchSrc));
  ucPrincipal ucprincipal_1 (
    .BranchSrc(BranchSrc), .opcode(decodificador_1_opcode), .MemWrite(MemWrite), .Branch(Branch),
    .out_12(Jalr), .ImmSrc(ImmSrc), .Jump(Jump), .RegWrite(RegWrite), .ALUOp(ALUOp), .ALUSrc(ALUSrc),
    .MemToReg(MemToReg), .Stop(Stop), .MemRead(MemRead), .PCSrc(PCSrc));
  // Probe on decodificador_1_rd
  Multiplexer #(.width(32)) multiplexer_3 (.in0(WD), .in1(PC_4_b16e401b), .out(multiplexer_3_out), .sel(Jump));
  ucULA ucula_1 (
    .funct7(decodificador_1_funct7), .funct3(decodificador_1_funct3), .ALUOp(ALUOp),
    .ALUControl(ucula_1_alucontrol));
  bancoRegistradores bancoregistradores_1 (
    .WD(multiplexer_3_out), .WR(decodificador_1_rd), .LD1(LD1), .LR1(decodificador_1_rs1),
    .LD2(bancoregistradores_1_ld2), .LR2(decodificador_1_rs2), .clk(CLK), .RegWrite(RegWrite));
  Multiplexer #(.width(32)) multiplexer_4 (.in0(bancoregistradores_1_ld2), .in1(Imm), .out(LD2), .sel(ALUSrc));
  ula ula_1 (.B(LD2), .ALUControl(ucula_1_alucontrol), .A(LD1), .NEG(Neg), .out_5(Zero), .Result(ALU));
  datamem datamem_1 (
    .Escreve_dado(bancoregistradores_1_ld2), .Endereco(ALU), .MemWrite(MemWrite), .clk(and_3_out),
    .MemRead(MemRead), .Dados_lidos(datamem_1_dados_lidos));  // open: clear
  and and_3 (and_3_out, CLK, ~Stop);  // AND_Gate
  Multiplexer #(.width(32)) multiplexer_5 (.in0(ALU), .in1(datamem_1_dados_lidos), .out(WD), .sel(MemToReg));

  // Notes on the sheet:
  //   Opcode
  //   rs1
  //   rs2
  //   rd
endmodule
