// Logisim project memdados.circ as structural Verilog: 1 circuit, main circuit datamem
// Mem. dados
module datamem (
  input  [31:0] Endereco,
  input  [31:0] Escreve_dado,
  input  clk,
  input  clear,
  input  MemWrite,
  input  MemRead,
  output [31:0] Dados_lidos
);

  RAM #(.addrWidth(24), .dataWidth(32), .trigger("falling")) ram_1 (
    .addr(Endereco[23:0]), .we(MemWrite), .oe(MemRead), .clk(clk), .din(Escreve_dado), .dout(Dados_lidos));
endmodule
