// Logisim project ucPrincipal.circ as structural Verilog: 1 circuit, main circuit ucPrincipal
module ucPrincipal (
  input  [6:0] opcode,
  input  BranchSrc,
  output RegWrite,
  output ALUSrcB,
  output PCSrc,
  output [2:0] ImmSrc,
  output [1:0] ALUOp,
  output [1:0] AluSrcA,
  output MemToReg,
  output MemRead,
  output MemWrite,
  output Branch,
  output Jalr,
  output Jump,
  output Stop
);

  wire and_1_out, E, I_type, Jal, R_type;

  and R (R_type, opcode[0], opcode[1], ~opcode[2], ~opcode[3], opcode[4], opcode[5], ~opcode[6]);  // AND_Gate
  and I (I_type, opcode[0], opcode[1], ~opcode[2], ~opcode[3], opcode[4], ~opcode[5], ~opcode[6]);  // AND_Gate
  and Load (MemRead, opcode[0], opcode[1], ~opcode[2], ~opcode[3], ~opcode[4], ~opcode[5], ~opcode[6]);  // AND_Gate
  and S (MemWrite, opcode[0], opcode[1], ~opcode[2], ~opcode[3], ~opcode[4], opcode[5], ~opcode[6]);  // AND_Gate
  and B (ALUOp[0], opcode[0], opcode[1], ~opcode[2], ~opcode[3], ~opcode[4], opcode[5], opcode[6]);  // AND_Gate
  and u_Jal (Jal, opcode[0], opcode[1], opcode[2], opcode[3], ~opcode[4], opcode[5], opcode[6]);  // AND_Gate
  and u_Jalr (Jalr, opcode[0], opcode[1], opcode[2], ~opcode[3], ~opcode[4], opcode[5], opcode[6]);  // AND_Gate
  and Lui (AluSrcA[0], opcode[0], opcode[1], opcode[2], ~opcode[3], opcode[4], opcode[5], ~opcode[6]);  // AND_Gate
  and Auipc (AluSrcA[1], opcode[0], opcode[1], opcode[2], ~opcode[3], opcode[4], ~opcode[5], ~opcode[6]);  // AND_Gate
  and u_E (E, opcode[0], opcode[1], ~opcode[2], ~opcode[3], opcode[4], opcode[5], opcode[6]);  // AND_Gate
  or or_1 (ALUOp[1], R_type, I_type);
  or or_2 (RegWrite, AluSrcA[0], Jal, Jalr, MemRead, I_type, R_type, AluSrcA[1]);
  or or_3 (ALUSrcB, AluSrcA[0], MemWrite, Jalr, MemRead, I_type, AluSrcA[1]);
  nor nor_1 (Stop, R_type, I_type, MemRead, MemWrite, ALUOp[0], Jal, Jalr, AluSrcA[0], AluSrcA[1], E);
  and and_1 (and_1_out, ALUOp[0], BranchSrc);
  or or_4 (PCSrc, Jal, and_1_out);
  or or_5 (ImmSrc[2], AluSrcA[1], AluSrcA[0]);
  or or_6 (ImmSrc[1], Jal, ALUOp[0]);
  or or_7 (ImmSrc[0], MemWrite, Jal);
  or or_8 (Jump, Jal, Jalr);

  assign Branch = ALUOp[0];
  assign MemToReg = MemRead;

  // Other names for the same wires on the sheet: B_type = ALUOp[0]; Lui = AluSrcA[0]; Auipc = AluSrcA[1];
  //   Load = MemRead; S_type = MemWrite

  // Notes on the sheet:
  //   0110011
  //   0010011
  //   0000011
  //   0100011
  //   1100011
  //   1101111
  //   1100111
  //   0110111
  //   1100111
  //   1110011
endmodule
